# Fritzing sketch wiring design (saved by Fritzing 0.9.5d)

parts:
  Part1 = Solar Panel [package="Renogy 50 Watts 12 Volt Monocrystalline Bendable Solar Panel"]
  U1 = ESP32-38PinWide [part_number=ESP32-38PinWide]
  A1 = drv-1012
  A2 = drv-1012
  M1 = DC Motor  # not connected
  M2 = DC Motor  # not connected
  BAT1 = 12 battery [package=battery]
  e-radionica_com1 = LM393 LDR breakout [part_number=100027]
  e-radionica_com2 = LM393 LDR breakout [part_number=100027]
  e-radionica_com3 = LM393 LDR breakout [part_number=100027]
  e-radionica_com4 = LM393 LDR breakout [part_number=100027]
  A3 = pzem-017
  J1 = XL4015 DC-DC CC CV module (blue)
  J2 = Camdenboss CTB0158-5 [part_number=CTB0158-5 package=THT]
  F1 = FUSE [package=fuse_5mm]
  J3 = Camdenboss CTB0158-5 [part_number=CTB0158-5 package=THT]
  RS485_module1 = RS485 Module (MAX3485)
  J4 = Camdenboss CTB0158-10 [part_number=CTB0158-10 package=THT]
  J5 = Camdenboss CTB0158-10 [part_number=CTB0158-10 package=THT]
  Mod1 = Solar Charge Controller [part_number="KLD Series Solar Charge Controller PWM" package=PWM-Model]

nets:
  N1: Part1.Connector_1, Mod1.Connector_1
  N2: Part1.Connector_2, Mod1.Connector_2
  N3: U1.GPIO33, A2.Pin_4
  N4: U1.GPIO25, A2.Pin_3
  N5: U1.GPIO26, A2.Pin_2
  N6: U1.GPIO27, A2.Pin_8
  N7: U1.GPIO14, A2.Pin_7
  N8: U1.GPIO12, A2.Pin_6
  N9: U1.GND, J5.terminal_7
  N10: U1.VIN, J4.terminal_7
  N11: U1.GPIO15, A1.Pin_8
  N12: U1.GPIO2, A1.Pin_7
  N13: U1.GPIO0, A1.Pin_4
  N14: U1.GPIO4, A1.Pin_3
  N15: U1.GPIO16, RS485_module1.DI
  N16: U1.GPIO17, RS485_module1.RO
  N17: U1.GPIO5, A1.Pin_2
  N18: U1.GPIO18, A1.Pin_6
  N19: U1.GPIO19, RS485_module1.RE, RS485_module1.DE
  N20: U1.GPIO21, e-radionica_com4.AO
  N21: U1.GPIO3, e-radionica_com3.AO
  N22: U1.GPIO1, e-radionica_com2.AO
  N23: U1.GPIO22, e-radionica_com1.AO
  N24: A1.Pin_1, J5.terminal_9
  N25: A1.Pin_5, J4.terminal_9
  N26: A1.Pin_11, J3.terminal_4
  N27: A1.Pin_12, J2.terminal_4
  N28: A2.Pin_1, J5.terminal_10
  N29: A2.Pin_5, J4.terminal_10
  N30: A2.Pin_11, J3.terminal_3
  N31: A2.Pin_12, J2.terminal_3
  N32: BAT1.+, F1.1
  N33: e-radionica_com1.VCC, J4.terminal_2
  N34: e-radionica_com1.GND, J5.terminal_2
  N35: e-radionica_com2.VCC, J4.terminal_3
  N36: e-radionica_com2.GND, J5.terminal_3
  N37: e-radionica_com3.VCC, J4.terminal_4
  N38: e-radionica_com3.GND, J5.terminal_4
  N39: e-radionica_com4.VCC, J4.terminal_5
  N40: e-radionica_com4.GND, J5.terminal_5
  N41: A3.Pin_1, J2.terminal_5
  N42: A3.Pin_2, J3.terminal_5
  N43: A3.Pin_5, RS485_module1.VCC
  N44: A3.Pin_6, RS485_module1.A
  N45: A3.Pin_7, RS485_module1.B
  N46: A3.Pin_8, RS485_module1.GND
  N47: J1.pin_2, J3.terminal_2
  N48: J1.pin_3, J4.terminal_1
  N49: J1.pin_4, J5.pin1, J5.pin10
  N50: J2.pin1, J2.pin5
  N51: J2.terminal_1, F1.2, Mod1.Connector_3
  N52: J3.pin1, J3.pin5
  N53: J3.terminal_1, Mod1.Connector_4
  N54: J4.pin1, J4.pin10

custom parts:
  Solar Panel: Renogy 50 Watts 12 Volt Solar Panel
  ESP32-38PinWide: Generic 38-Pin ESP32 with wide format (only access to one side of pins on a breadboard) based on Stephen Lilley's HiLetgo ESP-WROOM-32 ESP32 ESP-32S Development Board.
  drv-1012: .The BTS7960 is a fully integrated high current H bridge module for motor drive applications.
  12 battery: 12V lead acid type battery, like the Husqvarna YTH2448 12V 35AH battery. This is the mini version 1/4 the size of the actual battery to be closer to typical breadboard parts (around 2in wide rathher than 7in). The pads in pcb are sized to accomidate up to 14ga wire (as these batterys will deliver high currents.)
  pzem-017: PZEM-003/017 DC communication module, the module is mainly used for measuring DC voltage, current, active power, frequency and energy consumption, the module is without display function, the data is read through the RS485 interface.
  XL4015 DC-DC CC CV module (blue): XL4015 DC-DC CC/CV module blue
  RS485 Module (MAX3485): Commercially available RS485 to RS232 TTL Module
  Solar Charge Controller: PWM-Solar Charge Controller
